// Logisim project proj_2.circ as structural Verilog: 4 circuits, main circuit main
module main (
  input  in_1,
  input  in_2,
  input  in_3,
  input  in_4
);

  wire n2_bit_adder_1_c_0, n2_bit_adder_1_s_0, n2_bit_adder_1_s_1;
  wire [4:0] bin_led_driver_1_out_2, bin_led_driver_1_out_3, bin_led_driver_1_out_4, bin_led_driver_2_out_2,
       bin_led_driver_2_out_3, bin_led_driver_2_out_4, bin_led_driver_3_out_2, bin_led_driver_3_out_3,
       bin_led_driver_3_out_4, bin_led_driver_4_out_2, bin_led_driver_4_out_3, bin_led_driver_4_out_4,
       bin_led_driver_5_out_2, bin_led_driver_5_out_3, bin_led_driver_5_out_4, bin_led_driver_6_out_2,
       bin_led_driver_6_out_3, bin_led_driver_6_out_4, bin_led_driver_7_out_2, bin_led_driver_7_out_3,
       bin_led_driver_7_out_4;

  DotMatrix #(.matrixcols(3), .matrixrows(5)) dotmatrix_1 (
    .col0(bin_led_driver_1_out_2), .col1(bin_led_driver_1_out_3), .col2(bin_led_driver_1_out_4));
  bin_led_driver bin_led_driver_1 (
    .out_2(bin_led_driver_1_out_2), .out_3(bin_led_driver_1_out_3), .out_4(bin_led_driver_1_out_4),
    .in_1(in_1));
  DotMatrix #(.matrixcols(3), .matrixrows(5)) dotmatrix_2 (
    .col0(bin_led_driver_2_out_2), .col1(bin_led_driver_2_out_3), .col2(bin_led_driver_2_out_4));
  DotMatrix #(.matrixcols(3), .matrixrows(5)) dotmatrix_3 (
    .col0(bin_led_driver_3_out_2), .col1(bin_led_driver_3_out_3), .col2(bin_led_driver_3_out_4));
  bin_led_driver bin_led_driver_2 (
    .out_2(bin_led_driver_2_out_2), .out_3(bin_led_driver_2_out_3), .out_4(bin_led_driver_2_out_4),
    .in_1(in_2));
  bin_led_driver bin_led_driver_3 (
    .out_2(bin_led_driver_3_out_2), .out_3(bin_led_driver_3_out_3), .out_4(bin_led_driver_3_out_4),
    .in_1(in_3));
  DotMatrix #(.matrixcols(3), .matrixrows(5)) dotmatrix_4 (
    .col0(bin_led_driver_4_out_2), .col1(bin_led_driver_4_out_3), .col2(bin_led_driver_4_out_4));
  DotMatrix #(.matrixcols(3), .matrixrows(5)) dotmatrix_5 (
    .col0(bin_led_driver_6_out_2), .col1(bin_led_driver_6_out_3), .col2(bin_led_driver_6_out_4));
  bin_led_driver bin_led_driver_4 (
    .out_2(bin_led_driver_4_out_2), .out_3(bin_led_driver_4_out_3), .out_4(bin_led_driver_4_out_4),
    .in_1(in_4));
  _2_bit_adder u_2_bit_adder_1 (
    .a_1(in_1), .a_0(in_2), .b_1(in_3), .b_0(in_4), .c_i(1'b0), .s_1(n2_bit_adder_1_s_1),
    .s_0(n2_bit_adder_1_s_0), .c_0(n2_bit_adder_1_c_0));
  DotMatrix #(.matrixcols(3), .matrixrows(5)) dotmatrix_6 (
    .col0(bin_led_driver_7_out_2), .col1(bin_led_driver_7_out_3), .col2(bin_led_driver_7_out_4));
  DotMatrix #(.matrixcols(3), .matrixrows(5)) dotmatrix_7 (
    .col0(bin_led_driver_5_out_2), .col1(bin_led_driver_5_out_3), .col2(bin_led_driver_5_out_4));
  bin_led_driver bin_led_driver_5 (
    .out_2(bin_led_driver_5_out_2), .out_3(bin_led_driver_5_out_3), .out_4(bin_led_driver_5_out_4),
    .in_1(n2_bit_adder_1_s_0));
  bin_led_driver bin_led_driver_6 (
    .out_2(bin_led_driver_6_out_2), .out_3(bin_led_driver_6_out_3), .out_4(bin_led_driver_6_out_4),
    .in_1(n2_bit_adder_1_c_0));
  bin_led_driver bin_led_driver_7 (
    .out_2(bin_led_driver_7_out_2), .out_3(bin_led_driver_7_out_3), .out_4(bin_led_driver_7_out_4),
    .in_1(n2_bit_adder_1_s_1));
endmodule

module bin_led_driver (
  input  in_1,
  output [4:0] out_2,
  output [4:0] out_3,
  output [4:0] out_4
);

  not not_1 (out_2[3], in_1);
  DotMatrix #(.matrixcols(3), .matrixrows(5)) dotmatrix_1 (
    .col0({1'b1, {3{out_2[3]}}, 1'b1}), .col1({1'b1, {3{in_1}}, 1'b1}), .col2({{4{out_4[4]}}, 1'b1}));
  not not_2 (out_4[4], in_1);

  assign {out_2[4], out_2[2:0]} = {1'b1, {2{out_2[3]}}, 1'b1};
  assign out_3 = {1'b1, {3{in_1}}, 1'b1};
  assign out_4[3:0] = {{3{out_4[4]}}, 1'b1};
endmodule

module _2_bit_adder (
  input  a_1,
  input  a_0,
  input  b_1,
  input  b_0,
  input  c_i,
  output s_1,
  output s_0,
  output c_0
);

  wire n1_bit_adder_2_c_out;

  _1_bit_adder u_1_bit_adder_1 (.a(a_1), .b(b_1), .c_in(n1_bit_adder_2_c_out), .s(s_0), .c_out(c_0));
  _1_bit_adder u_1_bit_adder_2 (.a(a_0), .b(b_0), .c_in(c_i), .s(s_1), .c_out(n1_bit_adder_2_c_out));
endmodule

module _1_bit_adder (
  input  a,
  input  b,
  input  c_in,
  output s,
  output c_out
);

  wire nand_1_out, nand_2_out, nand_3_out, nand_4_out, nand_5_out, nand_6_out, nand_7_out;

  nand nand_1 (nand_1_out, a, b);
  nand nand_2 (nand_2_out, a, nand_1_out);
  nand nand_3 (nand_3_out, nand_1_out, b);
  nand nand_4 (nand_4_out, nand_2_out, nand_3_out);
  nand nand_5 (nand_5_out, nand_4_out, c_in);
  nand nand_6 (nand_6_out, nand_4_out, nand_5_out);
  nand nand_7 (nand_7_out, nand_5_out, c_in);
  nand nand_8 (c_out, nand_5_out, nand_1_out);
  nand nand_9 (s, nand_6_out, nand_7_out);
endmodule
